# Fritzing sketch 6 ignition drivers (saved by Fritzing 0.9.3b)
circuit board: 8.91203cm x 2.03478cm
breadboards: 1

parts:
  Q6 = Basic FET N-Channel [part_number="Bosch BIP373" package="TO220 [THT]"]
  Q5 = Basic FET N-Channel [part_number="Bosch BIP373" package="TO220 [THT]"]
  Q4 = Basic FET N-Channel [part_number="Bosch BIP373" package="TO220 [THT]"]
  Q3 = Basic FET N-Channel [part_number="Bosch BIP373" package="TO220 [THT]"]
  Q2 = Basic FET N-Channel [part_number="Bosch BIP373" package="TO220 [THT]"]
  Q1 = Basic FET N-Channel [part_number="Bosch BIP373" package="TO220 [THT]"]
  R6 = Resistor [tolerance=±5% resistance=680 part_number="RS-05K6800FT/RS-05K331JT (For 4 Cylinder)" package="0805 [SMD]"]
  R5 = Resistor [tolerance=±5% resistance=680 part_number="RS-05K6800FT/RS-05K331JT (For 4 Cylinder)" package="0805 [SMD]"]
  R4 = Resistor [tolerance=±5% resistance=680 part_number=RS-05K6800FT package="0805 [SMD]"]
  R3 = Resistor [tolerance=±5% resistance=680 part_number=RS-05K6800FT package="0805 [SMD]"]
  R2 = Resistor [tolerance=±5% resistance=680 part_number=RS-05K6800FT package="0805 [SMD]"]
  R1 = Resistor [tolerance=±5% resistance=680 part_number=RS-05K6800FT package="0805 [SMD]"]
  R7 = Resistor [tolerance=±5% resistance=7.5k part_number=CR-05JL7---7K5 package="0805 [SMD]"]
  pin56 = female pin header, 1 pin [form="♀ (female)"]
  pin27 = female pin header, 1 pin [form="♀ (female)"]
  pin26 = female pin header, 1 pin [form="♀ (female)"]
  D1 = Rectifier Diode [part_number=1N4001 breakdown_voltage=3.6V package="300 mil [THT]"]
  Q7 = NPN-Transistor [part_number=2SD596 package="SOT-23 [SMD]"]
  Q8 = NPN-Transistor [part_number=2SD596 package="SOT-23 [SMD]"]
  R10 = Resistor [tolerance=±5% resistance=1k part_number=RS-05K102JT package="0805 [SMD]"]
  tacho_in_mcu = female pin header, 1 pin [form="♀ (female)"]
  R8 = Resistor [tolerance=±5% resistance=10 part_number=RS-05K103JT package="0805 [SMD]"]
  tacho_out = female pin header, 1 pin [form="♀ (female)"]
  Q9 = NPN-Transistor [part_number=2SD596 package="SOT-23 [SMD]"]
  R11 = Resistor [tolerance=±5% resistance=7.5k part_number=CR-05JL7---7K5 package="0805 [SMD]"]
  ac_on_switch = female pin header, 1 pin [form="♀ (female)"]
  R9 = Resistor [tolerance=±5% resistance=10k part_number=RS-05K103JT package="0805 [SMD]"]
  AC_relay = female pin header, 1 pin [form="♀ (female)"]
  D2 = Rectifier Diode [part_number=1N4001 breakdown_voltage=3.6V package="300 mil [THT]"]
  Idle_up_mcu = female pin header, 1 pin [form="♀ (female)"]
  J13 = female pin header, 7 pins [form="♀ (female)"]
  J14 = female pin header, 20 pins [form="♀ (female)"]
  GND = female pin header, 1 pin [form="♀ (female)"]
  J12 = female pin header, 4 pins [form="♀ (female)"]
  J1 = Resistor [tolerance=±5% resistance=0 part_number="Solder Joint for 6 Cylinder" package="0805 [SMD]"]

nets:
  N1: Q6.gate, R6.Pin_0
  N2: Q6.drain, J13.pin2
  GND: Q6.source, Q5.source, Q4.source, Q3.source, Q2.source, Q1.source, Q7.2, Q8.2, Q9.2, J13.pin1, J14.pin1, J14.pin2, J14.pin3, J14.pin4, J14.pin5, J14.pin6, J14.pin7, J14.pin8, J14.pin9, J14.pin10, J14.pin11, J14.pin12, J14.pin13, J14.pin14, J14.pin15, J14.pin16, J14.pin17, J14.pin18, J14.pin19, J14.pin20, GND.pin1
  N3: Q5.gate, R5.Pin_0
  N4: Q5.drain, J13.pin3
  N5: Q4.gate, R4.Pin_0
  N6: Q4.drain, J13.pin4
  N7: Q3.gate, R3.Pin_0
  N8: Q3.drain, J13.pin5
  N9: Q2.gate, R2.Pin_0
  N10: Q2.drain, J13.pin6
  N11: Q1.gate, R1.Pin_0
  N12: Q1.drain, J13.pin7
  N13: R6.Pin_1, J12.pin4, J1.Pin_0
  N14: R5.Pin_1, J12.pin3, J1.Pin_1
  N15: R4.Pin_1, R3.Pin_1, J12.pin2
  N16: R2.Pin_1, R1.Pin_1, J12.pin1
  N17: R7.Pin_0, pin56.pin1, R8.Pin_1, R9.Pin_1
  N18: R7.Pin_1, Q7.0
  N19: pin27.pin1, D1.anode, Q7.1
  N20: pin26.pin1, D1.cathode
  N21: Q8.0, R10.Pin_1
  N22: Q8.1, R8.Pin_0, tacho_out.pin1
  N23: R10.Pin_0, tacho_in_mcu.pin1
  N24: Q9.0, R11.Pin_1
  N25: Q9.1, R9.Pin_0, AC_relay.pin1, D2.cathode
  N26: R11.Pin_0, ac_on_switch.pin1
  N27: D2.anode, Idle_up_mcu.pin1

notes:
  IGN1
  IGN2
  IGN3
  IGN1.1
  IGN1.2
  IGN2.1
  IGN2.2
  IGN3.1
  IGN3.2/4
  GND
  IGN4
